// Logisim project Lorrayne.circ as structural Verilog: 1 circuit, main circuit main
module main (
  input  p1,
  input  p2,
  input  p3,
  input  p4,
  output f,
  output a,
  output g,
  output b,
  output d,
  output e,
  output c
);

  wire and_1_out, and_2_out, and_3_out, and_4_out, and_5_out, and_6_out, and_7_out, and_8_out, not_1_out,
       not_2_out, not_3_out, not_4_out, not_5_out, not_6_out, not_7_out, not_8_out, not_9_out, not_10_out,
       not_11_out, not_12_out, not_13_out;

  not not_1 (not_1_out, p4);
  not not_2 (not_2_out, p3);
  and and_1 (and_1_out, not_2_out, not_3_out);
  not not_3 (not_3_out, p4);
  and and_2 (and_2_out, p2, not_4_out);
  not not_4 (not_4_out, p3);
  not not_5 (not_5_out, p3);
  and and_3 (and_3_out, not_5_out, not_6_out);
  not not_6 (not_6_out, p4);
  and and_4 (and_4_out, p2, not_7_out);
  not not_7 (not_7_out, p3);
  not not_8 (not_8_out, p2);
  and and_5 (and_5_out, not_8_out, not_9_out);
  not not_9 (not_9_out, p4);
  and and_6 (and_6_out, p2, not_10_out);
  not not_10 (not_10_out, p3);
  not not_11 (not_11_out, p2);
  and and_7 (and_7_out, not_11_out, not_12_out);
  not not_12 (not_12_out, p4);
  and and_8 (and_8_out, p2, not_13_out, p4);
  not not_13 (not_13_out, p3);
  or or_1 (a, not_1_out, p3, p2, p1);
  or or_2 (d, and_1_out, and_2_out, p1);
  or or_3 (e, and_3_out, and_4_out, p1);
  or or_4 (f, and_5_out, and_6_out, p1);
  or or_5 (g, and_7_out, and_8_out);
  _7_Segment_Display u_7_segment_display_1 (.g(g), .f(f), .a(a), .b(1'b1), .e(e), .d(d), .c(1'b1));  // open: dp

  assign b = 1'b1;
  assign c = 1'b1;
endmodule
